# Fritzing sketch Sketch (saved by Fritzing 0.9.3b)
breadboards: 1

parts:
  Part1 = Arduino Uno (Rev3)
  Part2 = Arduino Uno (Rev3)
  LED1 = LED - 5mm [color="Red (633nm)" package="5 mm [THT]"]
  R1 = Resistor [tolerance=±5% resistance=220 package=THT]
  R2 = Photocell (LDR) [package=THT]
  R3 = Resistor [tolerance=±5% resistance=220 package=THT]
  J1 = Piezo Speaker
  R4 = Resistor [tolerance=±5% resistance=220 package=THT]

nets:
  N1: Part1.A0, R2.pin_1, R3.Pin_0
  N2: Part1.5V, R2.pin_0
  N3: Part1.GND, R3.Pin_1
  N4: Part2.D11_PWM/MOSI, R4.Pin_1
  N5: Part2.D13/SCK, LED1.anode
  N6: Part2.GND, R1.Pin_0, J1.pin1
  N7: LED1.cathode, R1.Pin_1
  N8: J1.pin2, R4.Pin_0
